# Fritzing sketch project2 (saved by Fritzing 0.9.3b)
breadboards: 1

parts:
  IR1 = TSOP312.., 314.. [package=THT]
  KY-1 = Keyes Relay [package=THT]
  LED1 = LEDs [package=led10mm]
  Part1 = Arduino Uno (Rev3) - ICSP
  JP1 = Header 2 [package=screwterminal-3.5mm-2_lock]

nets:
  GND: IR1.GND, KY-1.ground, Part1.GND
  N1: IR1.Vs, KY-1.power, Part1.5V
  N2: IR1.Data, Part1.D7
  N3: KY-1.signal, Part1.D8
  N4: KY-1.NC, LED1.A
  N5: KY-1.C, JP1.1
  N6: LED1.C, JP1.2

custom parts:
  Keyes Relay: The Keyes 5V relay module is suitable for SCM development, home appliance control. It uses a 5V~12V TIL control signal which can control DC / AC signal.
  LEDs: LEDs Standard schematic elements and footprints for 5mm, 3mm, 1206, and 0603 sized LEDs. 5mm - Spark Fun Electronics SKU : COM-00529 (and others)
